// Logisim project MoleBuster-logisim2.circ as structural Verilog: 1 circuit, main circuit main
module main (
  input  enable,
  input  [2:0] led_index,
  output btn_pressed,
  output [2:0] btn_index
);

  wire B0_out, B1_out, B2_out, B3_out, decoder_1_out0, decoder_1_out1, decoder_1_out2, decoder_1_out3,
       decoder_1_out4, decoder_1_out5, decoder_1_out6, decoder_1_out7, priority_encoder_1_p6,
       priority_encoder_1_p8, priority_encoder_1_p9, priority_encoder_1_p10;

  LED L0 (.in(decoder_1_out0));
  Button B0 (.out(B0_out));
  Decoder #(.select(3)) decoder_1 (
    .out0(decoder_1_out0), .out1(decoder_1_out1), .out2(decoder_1_out2), .out3(decoder_1_out3),
    .out4(decoder_1_out4), .out5(decoder_1_out5), .out6(decoder_1_out6), .out7(decoder_1_out7),
    .sel(led_index), .en(enable));
  LED L3 (.in(decoder_1_out3));
  LED L2 (.in(decoder_1_out2));
  LED L1 (.in(decoder_1_out1));
  Button B3 (.out(B3_out));
  Button B2 (.out(B2_out));
  Button B1 (.out(B1_out));
  // Priority_Encoder priority_encoder_1: pin names not known; wires that end beside it: B0_out, B1_out, B2_out, B3_out, btn_index, priority_encoder_1_p6, btn_pressed, priority_encoder_1_p8, priority_encoder_1_p9, priority_encoder_1_p10
  LED L6 (.in(decoder_1_out6));
  LED L4 (.in(decoder_1_out4));
  LED L5 (.in(decoder_1_out5));
  Button B6 (.out(priority_encoder_1_p9));
  Button B4 (.out(priority_encoder_1_p6));
  Button B5 (.out(priority_encoder_1_p8));
  LED L7 (.in(decoder_1_out7));
  Button B7 (.out(priority_encoder_1_p10));
endmodule
