// Logisim project OpenTheGate.circ as structural Verilog: 1 circuit, main circuit main
module main (
);

  wire B_out, C_out, clock_1_out, init_out, not_1_out, not_2_out, not_3_out, not_4_out, O_out, s0, s1,
       undriven, undriven_2, undriven_3, undriven_4, V_out;

  Button B (.out(B_out));
  Button O (.out(O_out));
  Button C (.out(C_out));
  not not_1 (not_1_out, O_out);
  not not_2 (not_2_out, B_out);
  Button V (.out(V_out));
  not not_3 (not_3_out, C_out);
  not not_4 (not_4_out, V_out);
  Clock clock_1 (.out(clock_1_out));
  D_Flip_Flop State0 (.D(undriven), .clk(clock_1_out), .Q(s0));  // open: Qn, preset, reset
  D_Flip_Flop State1 (.D(undriven_2), .clk(clock_1_out), .Q(s1));  // open: Qn, preset, reset
  Button init (.out(init_out));
  LED U (.in(undriven_3));
  LED D (.in(undriven_4));

  // Notes on the sheet:
  //   Ajoutez ici des portes logiques
  //   pour réaliser la fonction de transition
  //   et la fonction de sortie
  //   Ajoutez des bascules et renommez-les
  //   de manière à respecter votre graphe d'états.
endmodule
